# Fritzing sketch collegamentiAuto (saved by Fritzing 0.9.2b)
breadboards: 1

parts:
  Componente1 = Arduino Uno (Rev3)
  IC2 = L293D [package=THT]
  M1 = DC Motor
  M2 = DC Motor
  VCC1 = 4 x AAA Battery Mount

nets:
  N1: Componente1.D10_PWM/SS, IC2.In_4
  N2: Componente1.D11_PWM/MOSI, IC2.In_3
  N3: Componente1.D3_PWM, IC2.In_1
  N4: Componente1.D4, IC2.In_2
  N5: Componente1.D6_PWM, IC2.Enable_2
  N6: Componente1.D7, IC2.Enable_1
  N7: Componente1.GND, IC2.0V, IC2.+Vmotor, VCC1.-, VCC1.+
  N8: IC2.Out_1_(_Controlled_by_Enable_1_), M2.pin_2
  N9: IC2.Out_2_(_Controlled_by_Enable_1_), M2.pin_1
  N10: IC2.Out_3_(_Controlled_by_Enable_2_), M1.pin_2
  N11: IC2.Out_4_(_Controlled_by_Enable_2_), M1.pin_1
